// Logisim project CS1410_U201414830_方成_cpu.circ as structural Verilog: 5 circuits, main circuit main
module main (
  output [9:0] R_type,
  output [9:0] I_type,
  output [5:0] J_type
);

  wire alu_1_equal, ALUsrc, and_1_out, and_2_out, and_3_out, and_4_out, and_5_out, beq, BLEZ, bne, Branch,
       clk, clock_1_out, Jal, jr, Jump, LUI, MemRead, MemtoReg, MemWrite, multiplexer_13_out, not_1_out,
       not_2_out, or_1_out, or_2_out, RegDst, RegWrite, shfit, syscall, Zero_Extend;
  wire [3:0] adder_1_out_2, OP_ALU;
  wire [4:0] multiplexer_1_out, multiplexer_2_out, multiplexer_3_out, multiplexer_4_out, multiplexer_5_out;
  wire [5:0] funct, OP;
  wire [11:0] counter_1_q;
  wire [25:6] rom_1_data;
  wire [27:0] adder_1_out, shifter_1_out;
  wire [31:0] a0, adder_2_out, alu_1_result, bit_extender_1_out, bit_extender_2_out, bit_extender_3_out,
       main_1_reg1, main_1_reg2_2, multiplexer_6_out, multiplexer_7_out, multiplexer_8_out,
       multiplexer_9_out, multiplexer_10_out, multiplexer_11_out, multiplexer_12_out, multiplexer_14_out,
       multiplexer_15_out, multiplexer_16_out, multiplexer_17_out, multiplexer_18_out, PC_q, ram_1_data,
       shifter_2_out, shifter_3_out;

  Register #(.width(32)) PC (.D(multiplexer_17_out), .Q(PC_q), .clk(clk));  // open: en, clr
  Hex_Digit_Display hex_digit_display_1 (.value(a0[31:28]));  // open: dp
  Adder #(.width(32)) adder_1 (.a(32'h4), .b(PC_q), .out({adder_1_out_2, adder_1_out}));  // open: cin, cout
  Hex_Digit_Display hex_digit_display_2 (.value(a0[23:20]));  // open: dp
  Hex_Digit_Display hex_digit_display_3 (.value(a0[27:24]));  // open: dp
  ROM #(.addrWidth(10), .dataWidth(32)) rom_1 (.addr(PC_q[11:2]), .data({OP, rom_1_data, funct}));  // open: sel
  Hex_Digit_Display hex_digit_display_4 (.value(a0[19:16]));  // open: dp
  Shifter #(.width(28)) shifter_1 (.in({OP[1:0], rom_1_data, funct}), .\dist (5'b00010), .out(shifter_1_out));
  Hex_Digit_Display hex_digit_display_5 (.value(a0[15:12]));  // open: dp
  Hex_Digit_Display hex_digit_display_6 (.value(a0[11:8]));  // open: dp
  Multiplexer #(.width(5), .enable("false")) multiplexer_1 (
    .in0(rom_1_data[25:21]), .in1(rom_1_data[20:16]), .out(multiplexer_1_out), .sel(shfit));
  Multiplexer #(.width(5), .enable("false")) multiplexer_2 (
    .in0(multiplexer_1_out), .in1({5{1'b1}}), .out(multiplexer_2_out), .sel(jr));
  Multiplexer #(.width(5), .enable("false")) multiplexer_3 (
    .in0(rom_1_data[20:16]), .in1(rom_1_data[15:11]), .out(multiplexer_3_out), .sel(RegDst));
  Hex_Digit_Display hex_digit_display_7 (.value(a0[3:0]));  // open: dp
  Hex_Digit_Display hex_digit_display_8 (.value(a0[7:4]));  // open: dp
  Multiplexer #(.width(5), .enable("false")) multiplexer_4 (
    .in0(multiplexer_2_out), .in1(5'b00010), .out(multiplexer_4_out), .sel(syscall));
  Multiplexer #(.width(5), .enable("false")) multiplexer_5 (
    .in0(multiplexer_3_out), .in1({5{1'b1}}), .out(multiplexer_5_out), .sel(Jal));
  assign bit_extender_1_out = {{16{rom_1_data[15]}}, {rom_1_data[15:6], funct}};  // Bit_Extender bit_extender_1
  assign bit_extender_2_out = {{16{1'b0}}, {rom_1_data[15:6], funct}};  // Bit_Extender bit_extender_2
  Multiplexer #(.width(32), .enable("false")) multiplexer_6 (
    .in0(multiplexer_8_out), .in1(multiplexer_9_out), .out(multiplexer_6_out), .sel(LUI));
  Multiplexer #(.width(32), .enable("false")) multiplexer_7 (
    .in0(bit_extender_1_out), .in1(bit_extender_2_out), .out(multiplexer_7_out), .sel(Zero_Extend));
  Shifter #(.width(32)) shifter_2 (.in(multiplexer_7_out), .\dist (5'b10000), .out(shifter_2_out));
  Multiplexer #(.width(32), .enable("false")) multiplexer_8 (
    .in0(multiplexer_18_out), .in1({adder_1_out_2, adder_1_out}), .out(multiplexer_8_out), .sel(Jal));
  // Probe on funct
  \CS1410_U201414830_方成_regfile_main  main_1 (
    .Reg1_num(multiplexer_4_out), .Reg2(rom_1_data[20:16]), .Write_Reg_num(multiplexer_5_out),
    .Din(multiplexer_6_out), .Write_Enable(RegWrite), .Clock(clk), .Reg1(main_1_reg1),
    .Reg2_2(main_1_reg2_2), .s0_Value(a0));  // open: s1_Value, s2_Value, ra_Value, ra_Value_2
  Multiplexer #(.width(32), .enable("false")) multiplexer_9 (
    .in0(multiplexer_7_out), .in1(shifter_2_out), .out(multiplexer_9_out), .sel(LUI));
  // Probe on OP
  Multiplexer #(.width(32), .enable("false")) multiplexer_10 (
    .in0(main_1_reg2_2), .in1(multiplexer_9_out), .out(multiplexer_10_out), .sel(ALUsrc));
  assign bit_extender_3_out = {{27{1'b0}}, rom_1_data[10:6]};  // Bit_Extender bit_extender_3
  Control_Unit control_unit_1 (
    .OP(OP), .funct(funct), .out_3(RegWrite), .out_4(ALUsrc), .out_5(MemWrite), .out_6(Branch),
    .out_7(MemtoReg), .out_8(Jal), .out_9(Zero_Extend), .out_10(MemRead), .out_11(bne), .out_12(Jump),
    .out_13(beq), .out_14(RegDst), .out_15(shfit), .out_16(jr), .out_17(syscall), .out_18(OP_ALU),
    .out_19(LUI), .out_20(BLEZ));
  Shifter #(.width(32)) shifter_3 (.in(multiplexer_9_out), .\dist (5'b00010), .out(shifter_3_out));
  and and_1 (and_1_out, Branch, or_1_out);
  or or_1 (or_1_out, and_2_out, and_3_out);
  and and_2 (and_2_out, bne, not_1_out);
  and and_3 (and_3_out, alu_1_equal, beq);
  not not_1 (not_1_out, alu_1_equal);
  Multiplexer #(.width(32), .enable("false")) multiplexer_11 (
    .in0(multiplexer_10_out), .in1(bit_extender_3_out), .out(multiplexer_11_out), .sel(shfit));
  Multiplexer #(.width(32), .enable("false")) multiplexer_12 (
    .in0(multiplexer_11_out), .in1(32'ha), .out(multiplexer_12_out), .sel(syscall));
  Adder #(.width(32)) adder_2 (
    .a({adder_1_out_2, adder_1_out}), .b(shifter_3_out), .out(adder_2_out));  // open: cin, cout
  Multiplexer #(.enable("false")) multiplexer_13 (
    .in0(and_1_out), .in1(and_4_out), .out(multiplexer_13_out), .sel(BLEZ));
  and and_4 (and_4_out, BLEZ, or_2_out);
  or or_2 (or_2_out, alu_1_equal, alu_1_result[0]);
  Multiplexer #(.width(32), .enable("false")) multiplexer_14 (
    .in0(multiplexer_12_out), .in1({32{1'b0}}), .out(multiplexer_14_out), .sel(BLEZ));
  Multiplexer #(.width(32), .enable("false")) multiplexer_15 (
    .in0({adder_1_out_2, adder_1_out}), .in1(adder_2_out), .out(multiplexer_15_out), .sel(multiplexer_13_out));
  ALU alu_1 (
    .AluOP(OP_ALU), .X(main_1_reg1), .Equal(alu_1_equal), .Result(alu_1_result), .Y(multiplexer_14_out));  // open: Signed_Overflow, Result_2, UnSigned_Overflow
  // Probe on OP_ALU
  Multiplexer #(.width(32), .enable("false")) multiplexer_16 (
    .in0(multiplexer_15_out), .in1({adder_1_out_2, shifter_1_out}), .out(multiplexer_16_out), .sel(Jump));
  Clock clock_1 (.out(clock_1_out));
  and and_5 (and_5_out, syscall, alu_1_equal);
  not not_2 (not_2_out, and_5_out);
  and and_6 (clk, clock_1_out, not_2_out);
  // Probe on R_type
  // Probe on I_type
  Instructtion_type instructtion_type_1 (.OP(OP), .clk(clk), .out_3(R_type), .out_4(I_type), .J_type(J_type));
  // Probe on J_type
  Multiplexer #(.width(32), .enable("false")) multiplexer_17 (
    .in0(multiplexer_16_out), .in1(main_1_reg1), .out(multiplexer_17_out), .sel(jr));
  // Probe on counter_1_q
  Counter #(.width(12), .max('hfff)) counter_1 (.Q(counter_1_q), .clk(clk));  // open: load, D, count, carry, clr
  RAM #(.addrWidth(24), .dataWidth(32), .bus("separate")) ram_1 (
    .addr(alu_1_result[25:2]), .din(main_1_reg2_2), .data(ram_1_data), .str(MemWrite), .clk(clk), .ld(MemRead));  // open: sel, clr
  Multiplexer #(.width(32), .enable("false")) multiplexer_18 (
    .in0(alu_1_result), .in1(ram_1_data), .out(multiplexer_18_out), .sel(MemtoReg));

  // Notes on the sheet:
  //   contents of rom_1 (hex, n*v repeats v):
  //   0 3c040001 3c040010 18000000
  //   rs
  //   rt
  //   rd
  //   shamt
  //   条件调转
  //   无条件调转
  //   jr
endmodule

module Control_Unit (
  input  [5:0] OP,
  input  [5:0] funct,
  output out_3,
  output out_4,
  output out_5,
  output out_6,
  output out_7,
  output out_8,
  output out_9,
  output out_10,
  output out_11,
  output out_12,
  output out_13,
  output out_14,
  output out_15,
  output out_16,
  output out_17,
  output [3:0] out_18,
  output out_19,
  output out_20
);

  wire Add, AddI, AddIU, AddU, AND, AndI, ARL, is_R, J, JR, multiplexer_1_out, Nor, nor_2_out, not_1_out,
       not_3_out, not_4_out, not_5_out, Or, or_6_out, OrI, Sll, Slt, SltI, SltU, SRA, Sub, XOR;
  wire [3:0] ALU_OP, multiplexer_3_out, multiplexer_4_out, multiplexer_5_out;

  R_Control r_control_1 (
    .funct5(funct[5]), .funct4(funct[4]), .funct3(funct[3]), .funct2(funct[2]), .funct1(funct[1]),
    .funct0(funct[0]), .Add(Add), .AddU(AddU), .AND(AND), .Sll(Sll), .SRA(SRA), .SRL(ARL), .Sub(Sub),
    .Or(Or), .Nor(Nor), .Slt(Slt), .SltU(SltU), .JR(JR), .XOR(XOR));
  I_Control i_control_1 (
    .OP5(OP[5]), .OP4(OP[4]), .OP3(OP[3]), .OP2(OP[2]), .OP1(OP[1]), .OP0(OP[0]), .AddI(AddI), .AddIU(AddIU),
    .AndI(AndI), .OrI(OrI), .Lw(out_7), .Sw(out_5), .Beq(out_13), .Bne(out_11), .SltI(SltI), .J(J),
    .JAL(out_8), .LUI(out_19), .BLEZ(out_20));
  or or_1 (out_4, AddI, AddIU, AndI, OrI, out_7, out_5, SltI);
  or or_2 (out_12, J, out_8);
  or or_3 (out_6, out_13, out_20, out_11);
  not not_1 (not_1_out, funct[5]);
  and and_1 (out_15, is_R, not_1_out, multiplexer_1_out);
  nor nor_1 (out_14, OP[5], OP[4], OP[3], OP[2], OP[1], OP[0]);
  Multiplexer #(.select(2), .enable("false")) multiplexer_1 (
    .in0(1'b1), .in2(1'b1), .in3(1'b1), .out(multiplexer_1_out), .sel(funct[1:0]));  // open: in1
  or or_4 (out_9, AndI, AddIU, OrI);
  Multiplexer #(.select(4), .width(4), .enable("false")) multiplexer_2 (
    .in0(4'b0000), .in1(4'b1111), .in2(4'b1111), .in3(4'b0101), .in4(4'b0101), .in5(4'b0101), .in6(4'b1011),
    .in7(4'b1111), .in8(4'b0101), .in9(4'b0101), .in10(4'b1011), .in11(4'b0101), .in12(4'b0111),
    .in13(4'b1000), .in14(4'b1111), .in15(4'b1111), .out(ALU_OP), .sel(OP[3:0]));
  Multiplexer #(.select(2), .width(4), .enable("false")) multiplexer_3 (
    .in0(4'b0000), .in2(4'b0010), .in3(4'b0001), .out(multiplexer_3_out), .sel(funct[1:0]));  // open: in1
  Multiplexer #(.select(4), .width(4), .enable("false")) multiplexer_4 (
    .in0(4'b0101), .in1(4'b0101), .in2(4'b0110), .in3(4'b1111), .in4(4'b0111), .in5(4'b1000), .in6(4'b1001),
    .in7(4'b1010), .in8(4'b1111), .in9(4'b1111), .in10(4'b1011), .in11(4'b1100), .in12(4'b1111),
    .in13(4'b1111), .in14(4'b1111), .in15(4'b1111), .out(multiplexer_4_out), .sel(funct[3:0]));
  // Probe on ALU_OP
  Multiplexer #(.width(4), .enable("false")) multiplexer_5 (
    .in0(multiplexer_3_out), .in1(multiplexer_4_out), .out(multiplexer_5_out), .sel(funct[5]));
  or or_5 (out_3, out_14, AddI, AddIU, AndI, out_8, SltI, out_7, OrI, out_19);
  or or_6 (or_6_out, ALU_OP[3], ALU_OP[2], ALU_OP[1], ALU_OP[0]);
  not not_2 (is_R, or_6_out);
  // Probe on out_18
  Multiplexer #(.width(4), .enable("false")) multiplexer_6 (
    .in0(multiplexer_5_out), .in1(ALU_OP), .out(out_18), .sel(not_3_out));
  not not_3 (not_3_out, is_R);
  and and_2 (out_16, is_R, JR);
  and and_3 (out_17, is_R, nor_2_out);
  not not_4 (not_4_out, funct[3]);
  not not_5 (not_5_out, funct[2]);
  nor nor_2 (nor_2_out, funct[5], funct[4], not_4_out, not_5_out, funct[1], funct[0]);

  assign out_10 = out_7;

  // Other names for the same wires on the sheet: ALUsrc = out_4; Beq = out_13; BLEZ = out_20; Bne = out_11;
  //   Branch = out_6; f2_f1[1:0] = funct[1:0]; f4_f1[3:0] = funct[3:0]; f6 = funct[5]; JAL = out_8; jr_t = out_16;
  //   Jump = out_12; LUI = out_19; Lw = out_7; MemRead = out_7; MemtoReg = out_7; op_t[3:0] = OP[3:0];
  //   OP_ALU[3:0] = out_18; R_type = out_14; RegDst = out_14; RegWrite = out_3; shfit = out_15; MemWrite = out_5;
  //   Sw = out_5; syscall = out_17; Zero_Extend = out_9

  // Notes on the sheet:
  //   shift
endmodule

module R_Control (
  input  funct5,
  input  funct4,
  input  funct3,
  input  funct2,
  input  funct1,
  input  funct0,
  output Add,
  output AddU,
  output AND,
  output Sll,
  output SRA,
  output SRL,
  output Sub,
  output Or,
  output Nor,
  output Slt,
  output SltU,
  output JR,
  output XOR
);

  wire not_1_out, not_2_out, not_3_out, not_4_out, not_5_out, not_6_out, not_7_out, not_8_out, not_9_out,
       not_10_out, not_11_out, not_12_out, not_13_out, not_14_out, not_15_out, not_16_out, not_17_out,
       not_18_out, not_19_out, not_20_out, not_21_out, not_22_out, not_23_out, not_24_out, not_25_out,
       not_26_out, not_27_out, not_28_out, not_29_out, not_30_out, not_31_out, not_32_out, not_33_out,
       not_34_out, not_35_out, not_36_out, not_37_out, not_38_out, not_39_out, not_40_out, not_41_out,
       not_42_out, not_43_out, not_44_out, not_45_out, not_46_out, not_47_out, not_48_out, not_49_out,
       not_50_out;

  not not_1 (not_1_out, funct4);
  not not_2 (not_2_out, funct3);
  not not_3 (not_3_out, funct2);
  not not_4 (not_4_out, funct1);
  not not_5 (not_5_out, funct0);
  not not_6 (not_6_out, funct4);
  not not_7 (not_7_out, funct3);
  not not_8 (not_8_out, funct2);
  not not_9 (not_9_out, funct1);
  not not_10 (not_10_out, funct4);
  not not_11 (not_11_out, funct3);
  not not_12 (not_12_out, funct1);
  not not_13 (not_13_out, funct0);
  not not_14 (not_14_out, funct5);
  not not_15 (not_15_out, funct4);
  not not_16 (not_16_out, funct3);
  not not_17 (not_17_out, funct2);
  not not_18 (not_18_out, funct1);
  not not_19 (not_19_out, funct0);
  not not_20 (not_20_out, funct5);
  not not_21 (not_21_out, funct4);
  not not_22 (not_22_out, funct3);
  not not_23 (not_23_out, funct2);
  not not_24 (not_24_out, funct5);
  not not_25 (not_25_out, funct4);
  not not_26 (not_26_out, funct3);
  not not_27 (not_27_out, funct2);
  not not_28 (not_28_out, funct0);
  not not_29 (not_29_out, funct4);
  not not_30 (not_30_out, funct3);
  not not_31 (not_31_out, funct2);
  not not_32 (not_32_out, funct0);
  not not_33 (not_33_out, funct4);
  not not_34 (not_34_out, funct3);
  not not_35 (not_35_out, funct1);
  not not_36 (not_36_out, funct4);
  not not_37 (not_37_out, funct3);
  not not_38 (not_38_out, funct4);
  not not_39 (not_39_out, funct2);
  not not_40 (not_40_out, funct0);
  not not_41 (not_41_out, funct4);
  not not_42 (not_42_out, funct2);
  not not_43 (not_43_out, funct5);
  not not_44 (not_44_out, funct4);
  not not_45 (not_45_out, funct2);
  not not_46 (not_46_out, funct1);
  not not_47 (not_47_out, funct0);
  not not_48 (not_48_out, funct4);
  not not_49 (not_49_out, funct3);
  not not_50 (not_50_out, funct0);
  and and_1 (Add, funct5, not_1_out, not_2_out, not_3_out, not_4_out, not_5_out);
  and and_2 (AddU, funct5, not_6_out, not_7_out, not_8_out, not_9_out, funct0);
  and and_3 (AND, funct5, not_10_out, not_11_out, funct2, not_12_out, not_13_out);
  and and_4 (Sll, not_14_out, not_15_out, not_16_out, not_17_out, not_18_out, not_19_out);
  and and_5 (SRA, not_20_out, not_21_out, not_22_out, not_23_out, funct1, funct0);
  and and_6 (SRL, not_24_out, not_25_out, not_26_out, not_27_out, funct1, not_28_out);
  and and_7 (Sub, funct5, not_29_out, not_30_out, not_31_out, funct1, not_32_out);
  and and_8 (Or, funct5, not_33_out, not_34_out, funct2, not_35_out, funct0);
  and and_9 (Nor, funct5, not_36_out, not_37_out, funct2, funct1, funct0);
  and and_10 (Slt, funct5, not_38_out, funct3, not_39_out, funct1, not_40_out);
  and and_11 (SltU, funct5, not_41_out, funct3, not_42_out, funct1, funct0);
  and and_12 (JR, not_43_out, not_44_out, funct3, not_45_out, not_46_out, not_47_out);
  and and_13 (XOR, funct5, not_48_out, not_49_out, funct2, funct1, not_50_out);
endmodule

module I_Control (
  input  OP5,
  input  OP4,
  input  OP3,
  input  OP2,
  input  OP1,
  input  OP0,
  output AddI,
  output AddIU,
  output AndI,
  output OrI,
  output Lw,
  output Sw,
  output Beq,
  output Bne,
  output SltI,
  output J,
  output JAL,
  output LUI,
  output BLEZ
);

  wire not_1_out, not_2_out, not_3_out, not_4_out, not_5_out, not_6_out, not_7_out, not_8_out, not_9_out,
       not_10_out, not_11_out, not_12_out, not_13_out, not_14_out, not_15_out, not_16_out, not_17_out,
       not_18_out, not_19_out, not_20_out, not_21_out, not_22_out, not_23_out, not_24_out, not_25_out,
       not_26_out, not_27_out, not_28_out, not_29_out, not_30_out, not_31_out, not_32_out, not_33_out,
       not_34_out, not_35_out, not_36_out, not_37_out, not_38_out, not_39_out, not_40_out, not_41_out,
       not_42_out, not_43_out, not_44_out, not_45_out, not_46_out, not_47_out, not_48_out, not_49_out;

  not not_1 (not_1_out, OP5);
  not not_2 (not_2_out, OP4);
  not not_3 (not_3_out, OP2);
  not not_4 (not_4_out, OP1);
  not not_5 (not_5_out, OP0);
  not not_6 (not_6_out, OP5);
  not not_7 (not_7_out, OP4);
  not not_8 (not_8_out, OP2);
  not not_9 (not_9_out, OP1);
  not not_10 (not_10_out, OP5);
  not not_11 (not_11_out, OP4);
  not not_12 (not_12_out, OP1);
  not not_13 (not_13_out, OP0);
  not not_14 (not_14_out, OP5);
  not not_15 (not_15_out, OP4);
  not not_16 (not_16_out, OP1);
  not not_17 (not_17_out, OP4);
  not not_18 (not_18_out, OP3);
  not not_19 (not_19_out, OP2);
  not not_20 (not_20_out, OP4);
  not not_21 (not_21_out, OP2);
  not not_22 (not_22_out, OP5);
  not not_23 (not_23_out, OP4);
  not not_24 (not_24_out, OP3);
  not not_25 (not_25_out, OP1);
  not not_26 (not_26_out, OP0);
  not not_27 (not_27_out, OP5);
  not not_28 (not_28_out, OP4);
  not not_29 (not_29_out, OP3);
  not not_30 (not_30_out, OP1);
  not not_31 (not_31_out, OP5);
  not not_32 (not_32_out, OP4);
  not not_33 (not_33_out, OP2);
  not not_34 (not_34_out, OP0);
  not not_35 (not_35_out, OP5);
  not not_36 (not_36_out, OP4);
  not not_37 (not_37_out, OP3);
  not not_38 (not_38_out, OP2);
  not not_39 (not_39_out, OP0);
  not not_40 (not_40_out, OP5);
  not not_41 (not_41_out, OP4);
  not not_42 (not_42_out, OP3);
  not not_43 (not_43_out, OP2);
  not not_44 (not_44_out, OP5);
  not not_45 (not_45_out, OP4);
  not not_46 (not_46_out, OP5);
  not not_47 (not_47_out, OP4);
  not not_48 (not_48_out, OP3);
  not not_49 (not_49_out, OP0);
  and and_1 (AddI, not_1_out, not_2_out, OP3, not_3_out, not_4_out, not_5_out);
  and and_2 (AddIU, not_6_out, not_7_out, OP3, not_8_out, not_9_out, OP0);
  and and_3 (AndI, not_10_out, not_11_out, OP3, OP2, not_12_out, not_13_out);
  and and_4 (OrI, not_14_out, not_15_out, OP3, OP2, not_16_out, OP0);
  and and_5 (Lw, OP5, not_17_out, not_18_out, not_19_out, OP1, OP0);
  and and_6 (Sw, OP5, not_20_out, OP3, not_21_out, OP1, OP0);
  and and_7 (Beq, not_22_out, not_23_out, not_24_out, OP2, not_25_out, not_26_out);
  and and_8 (Bne, not_27_out, not_28_out, not_29_out, OP2, not_30_out, OP0);
  and and_9 (SltI, not_31_out, not_32_out, OP3, not_33_out, OP1, not_34_out);
  and and_10 (J, not_35_out, not_36_out, not_37_out, not_38_out, OP1, not_39_out);
  and and_11 (JAL, not_40_out, not_41_out, not_42_out, not_43_out, OP1, OP0);
  and and_12 (LUI, not_44_out, not_45_out, OP3, OP2, OP1, OP0);
  and and_13 (BLEZ, not_46_out, not_47_out, not_48_out, OP2, OP1, not_49_out);
endmodule

module Instructtion_type (
  input  [5:0] OP,
  input  clk,
  output [9:0] out_3,
  output [9:0] out_4,
  output [5:0] J_type
);

  wire nor_1_out, nor_2_out, nor_3_out, not_1_out, not_2_out, not_3_out, not_4_out, not_5_out, or_1_out,
       subtractor_1_bout;
  wire [9:0] counter_1_q;

  Subtractor #(.width(6)) subtractor_1 (.a(OP), .b(6'b000011), .bout(subtractor_1_bout));  // open: out, bin
  not not_1 (not_1_out, OP[0]);
  not not_2 (not_2_out, OP[1]);
  nor nor_1 (nor_1_out, OP[0], OP[1], OP[2], OP[3], OP[4], OP[5]);
  nor nor_2 (nor_2_out, not_1_out, not_2_out, OP[2], OP[3], OP[4], OP[5]);
  nor nor_3 (nor_3_out, OP[0], not_2_out, OP[2], OP[3], OP[4], OP[5]);
  not not_3 (not_3_out, subtractor_1_bout);
  or or_1 (or_1_out, nor_2_out, nor_3_out);
  not not_4 (not_4_out, nor_1_out);
  Counter #(.width(10), .max('h3ff)) counter_1 (
    .load(not_4_out), .D(counter_1_q), .count(nor_1_out), .Q(counter_1_q), .clk(clk));  // open: carry, clr
  Counter #(.width(10), .max('h3ff)) counter_2 (
    .load(subtractor_1_bout), .D(out_4), .count(not_3_out), .Q(out_4), .clk(clk));  // open: carry, clr
  not not_5 (not_5_out, or_1_out);
  Counter #(.width(6), .max('h3f)) counter_3 (
    .load(not_5_out), .D(J_type), .count(or_1_out), .Q(J_type), .clk(clk));  // open: carry, clr
  Adder #(.width(10)) adder_1 (.a(counter_1_q), .b(10'h1), .out(out_3));  // open: cin, cout
endmodule
